// Logisim project Gated_D_Latch.circ as structural Verilog: 1 circuit, main circuit main
module main (
  input  Enable,
  input  Swap_Sides,
  output out_3,
  output out_4
);

  wire and_1_out, and_2_out, not_1_out;

  not not_1 (not_1_out, Swap_Sides);
  and and_1 (and_1_out, not_1_out, Enable);
  and and_2 (and_2_out, Enable, Swap_Sides);
  nor nor_1 (out_3, and_1_out, out_4);
  nor nor_2 (out_4, out_3, and_2_out);
endmodule
