// Logisim project Logic_Gates.circ as structural Verilog: 1 circuit, main circuit main
module main (
  input  in_1,
  input  in_2,
  input  in_3,
  output out_4,
  output out_5
);

  wire transistor_3_out;

  Transistor transistor_1 (.in(1'b1), .out(out_4), .gate(in_2));
  Transistor #(.\type ("n")) transistor_2 (.in(1'b0), .out(out_4), .gate(in_2));
  Transistor transistor_3 (.in(1'b1), .out(transistor_3_out), .gate(in_1));
  Transistor transistor_4 (.in(transistor_3_out), .out(in_1), .gate(in_3));
  Transistor #(.\type ("n")) transistor_5 (.gate(in_1));  // open: in, out
  Transistor #(.\type ("n")) transistor_6 (.out(in_1), .gate(in_3));  // open: in

  assign out_5 = in_1;

  // Notes on the sheet:
  //   Control Voltage
  //   Nor Gate
endmodule
